# Fritzing sketch conexionArduinoKeypad (saved by Fritzing 0.9.3b)

parts:
  Componente1 = Arduino Mega 2560 (Rev3)
  Matrix_keypad1 = KEYPAD 4x4

nets:
  N1: Componente1.D22, Matrix_keypad1.row4
  N2: Componente1.D23, Matrix_keypad1.row3
  N3: Componente1.D24, Matrix_keypad1.row2
  N4: Componente1.D25, Matrix_keypad1.row1
  N5: Componente1.D26, Matrix_keypad1.col4
  N6: Componente1.D27, Matrix_keypad1.col3
  N7: Componente1.D28, Matrix_keypad1.col2
  N8: Componente1.D29, Matrix_keypad1.col1

custom parts:
  KEYPAD 4x4: Matrix keypad 16 buttons, 4 rows x 4 columns
