# Fritzing sketch conexionArduinoLCD (saved by Fritzing 0.9.3b)

parts:
  Pantalla_LCD_Midas = LCD1602-I2C
  Componente2 = Arduino Mega 2560 (Rev3)
  Potenciómetro = Trimmer Potentiometer [maximum_resistance=10kΩ package=THT]

nets:
  N1: Pantalla_LCD_Midas.DB7, Componente2.D35
  N2: Pantalla_LCD_Midas.DB6, Componente2.D34
  N3: Pantalla_LCD_Midas.DB5, Componente2.D33
  N4: Pantalla_LCD_Midas.DB4, Componente2.D32
  N5: Pantalla_LCD_Midas.E1, Componente2.D36
  N6: Pantalla_LCD_Midas.RS, Componente2.D38
  N7: Pantalla_LCD_Midas.V0, Potenciómetro.wiper
  VSS: Pantalla_LCD_Midas.Vss, Componente2.GND
  VDD: Pantalla_LCD_Midas.Vdd, Componente2.5V
  N8: Pantalla_LCD_Midas.E2, Componente2.D37

custom parts:
  LCD1602-I2C: A standard character display, usually with 2x16 characters. Comes in many colors with LCM1602 IIC attached.
