# Fritzing sketch esquema lcd (saved by Fritzing 0.9.3b)

parts:
  LCD1 = LCD screen
  part = Rotary Potentiometer (Small) [maximum_resistance=100kΩ]  # not connected
  U1 = Arduino Mega 2560 (Rev3)  # not connected
  R1 = Rotary Potentiometer (Small) [maximum_resistance=100kΩ package=THT]

nets:
  N1: LCD1.DB5, R1.wiper
  N2: LCD1.DB6, R1.leg1
